# Fritzing sketch sketch (saved by Fritzing 0.9.5d)
breadboards: 1

parts:
  Arduino_Nano = Arduino Nano (Rev3.0)
  Photoresistor = Photocell (LDR) [package=THT]
  R2 = Resistor [tolerance=±20% resistance=10k package=THT]
  TLE4906_Hall_sensor = mystery part, 3 pins [chip_label=TLE4906]
  R3 = Resistor [tolerance=±20% resistance=10k package=THT]
  R4 = Resistor [tolerance=±5% resistance=220 package=THT]
  16x2_LCD = LCD-16X2 [package=lcd-16x2_noholes]
  LCM1602_IIC2 = LCM1602 IIC [part_number="LCM1602 IIC" chip_label="LCM1602 IIC" package="DIP (Dual Inline) [THT]"]
  LM35 = LM35 Temperature Sensor [package="TO92 [THT]"]

nets:
  N1: Arduino_Nano.D2, R2.Pin_1, TLE4906_Hall_sensor.pin3
  N2: Arduino_Nano.D3, R4.Pin_0
  GND: Arduino_Nano.GND, TLE4906_Hall_sensor.pin2, R3.Pin_0, LCM1602_IIC2.GND, LM35.GND
  5V: Arduino_Nano.5V, Photoresistor.pin_1, R2.Pin_0, TLE4906_Hall_sensor.pin1, LCM1602_IIC2.VCC, LM35.+Vs
  N3: Arduino_Nano.A5, LCM1602_IIC2.SCL
  N4: Arduino_Nano.A4, LCM1602_IIC2.SDA
  N5: Arduino_Nano.A3, LM35.Vout
  N6: Arduino_Nano.A0, Photoresistor.pin_0, R3.Pin_1
  N7: R4.Pin_1, 16x2_LCD.A
  VSS: 16x2_LCD.VSS, LCM1602_IIC2.VSS
  VDD: 16x2_LCD.VDD, LCM1602_IIC2.VDD
  N8: 16x2_LCD.VO, LCM1602_IIC2.V0
  N9: 16x2_LCD.RS, LCM1602_IIC2.RS
  N10: 16x2_LCD.R_W, LCM1602_IIC2.RW
  N11: 16x2_LCD.E, LCM1602_IIC2.E
  N12: 16x2_LCD.DB4, LCM1602_IIC2.D4
  N13: 16x2_LCD.DB5, LCM1602_IIC2.D5
  N14: 16x2_LCD.DB6, LCM1602_IIC2.D6
  N15: 16x2_LCD.DB7, LCM1602_IIC2.D7
  N16: 16x2_LCD.K, LCM1602_IIC2.K

custom parts:
  LCM1602 IIC: I2C-Module to use a 1602 or 2004 LCD on with the wire.h libory Serial LCD Modul
